# Fritzing sketch team3_demo (saved by Fritzing 0.9.3b)

parts:
  Composant1 = Arduino Uno (Rev3) - ICSP
  NEOPIXEL1 = Neopixel Strip -- Black (30/m) [part_number=1376]
  C1 = Electrolytic Capacitor [capacitance=100µF package="200 mil [THT, electrolytic]"]  # not connected
  MP3-1 = Serial MP3 Player
  J1 = Basic Servo
  S1 = Round Pushbutton
  R1 = Resistor [tolerance=±5% resistance=220 package=THT]

nets:
  N1: Composant1.D8, R1.Pin_0
  N2: Composant1.D1/TX, MP3-1.pin4
  N3: Composant1.D5_PWM, S1.leg1
  5V: Composant1.5V, NEOPIXEL1.+5V, MP3-1.pin2, J1.vcc
  GND: Composant1.GND, NEOPIXEL1.GND, MP3-1.pin1, J1.gnd
  N4: NEOPIXEL1.Din, R1.Pin_1

custom parts:
  Neopixel Strip -- Black (30/m): These NeoPixel strips have 30 digitally-addressable pixel LEDs per meter and are very affordable and are only 12.5 mm wide, 10 mm if you remove the strip from the casing.
  Serial MP3 Player: The module is a kind of simple MP3 player device which is based on a high-quality MP3 audio chip---YX5300. It can support 8k Hz ~ 48k Hz sampling frequency MP3 and WAV file formats. There is a TF card socket on board, so you can plug the micro SD card that stores audio files. MCU can control the MP3 playback state by sending commands to the module via UART port, such as switch songs, change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
